# Fritzing sketch 8d5a105f-6e61-46d1-a160-2962547bdaee (saved by Fritzing 0.9.3b)
breadboards: 1

parts:
  WeMos_D1_Mini1 = WeMos D1 Mini
  S1 = Pushbutton [package="[THT]"]
  S2 = Pushbutton [package="[THT]"]
  U1 = SWITCH-SPST-2 [package=switch-spst-vertical]
  SPKR1 = Loudspeaker  # not connected
  MIC1 = Microphone  # not connected
  U2 = LIPO-1000mAh [package=lipo-1000]
  R1 = Resistor [tolerance=±5% resistance=220 package="0402 [SMD]"]
  R2 = Resistor [tolerance=±5% resistance=220 package="0402 [SMD]"]

nets:
  N1: WeMos_D1_Mini1.3V3, U1.P
  N2: WeMos_D1_Mini1.D1, R1.Pin_0
  N3: WeMos_D1_Mini1.D4, R2.Pin_0
  N4: WeMos_D1_Mini1.G, S1.Pin_3, S1.Pin_4, S2.Pin_3, S2.Pin_4, U2.-, R1.Pin_1, R2.Pin_1
  N5: S1.Pin_1, S1.Pin_2, S2.Pin_1, S2.Pin_2, U1.O, U2.+
